# Fritzing sketch porsche (saved by Fritzing 0.8.0b)
breadboards: 1

parts:
  Part3 = Arduino Nano (Rev3.0)
  IC1 = IC, DIP package, 28 pins [chip_label=TLC5940N]
  J1 = shrouded pin header, 8 pins [form="♂ (shrouded male)"]
  R1 = Resistor [tolerance=±5% resistance=2.2k package=THT]
  R2 = Resistor [tolerance=±5% resistance=10k package=THT]
  VCC1 = Battery block 9V

nets (from the breadboard view):
  N1: Part3.D7, J1.pin3
  N2: Part3.D8, J1.pin6
  N3: Part3.D9, IC1.pin24
  N4: Part3.D10, IC1.pin23, R2.Pin_0
  N5: Part3.D11/MOSI, IC1.pin26, J1.pin2
  N6: Part3.D12/MISO, J1.pin8
  N7: Part3.VIN, IC1.pin19, IC1.pin21, J1.pin4, J1.pin5, R2.Pin_1, VCC1.+
  N8: Part3.GND, IC1.pin22, IC1.pin27, R1.Pin_1, VCC1.-
  N9: Part3.D13/SCK, IC1.pin25, J1.pin7
  N10: IC1.pin20, R1.Pin_0

notes:
  NRF24L01+:
  MISO->12
  MOSI -> 11
  SCK -> 13
  CE -> 8
  CSN ->7
  1 -> GND
  2 -> Vcc
  3 -> CE -> 8
  4 -> CSN -> 7
  5 -> SCK -> 13
  6 -> MOSI -> 11
  7 -> MISO -> 12
  8-> IRQ -> N/A
