# Fritzing sketch car controller (saved by Fritzing 0.7.4b)
breadboards: 1

parts:
  Arduino1 = Arduino Nano v2.3
  J1 = female pin header, 2 pins [form="♀ (female)"]
  J2 = shrouded pin header, 8 pins [form="♂ (shrouded male)"]
  J3 = shrouded pin header, 10 pins [form="♂ (shrouded male)"]
  Q3 = Basic FET P-Channel [package="TO220 [THT]"]
  Q4 = Basic FET P-Channel [package="TO220 [THT]"]
  Q1 = Basic FET N-Channel [package="TO220 [THT]"]
  Q2 = Basic FET N-Channel [package="TO220 [THT]"]
  D1 = Rectifier Diode [part_number=1N4001 package="300 mil [THT]"]
  J4 = female pin header, 2 pins [form="♀ (female)"]
  D2 = Rectifier Diode [part_number=1N4001 package="300 mil [THT]"]
  D3 = Rectifier Diode [part_number=1N4001 package="300 mil [THT]"]
  D4 = Rectifier Diode [part_number=1N4001 package="300 mil [THT]"]

nets:
  N1: Arduino1.GND, J1.pin1, J2.pin1, J3.pin10, Q3.source, Q4.source, D2.anode, D3.anode
  N2: Arduino1.D3, J3.pin2
  N3: Arduino1.D5, J3.pin3
  N4: Arduino1.D6, J3.pin4
  N5: Arduino1.D7, J2.pin7
  N6: Arduino1.D8, J2.pin3
  N7: Arduino1.D9, J2.pin4
  N8: Arduino1.D10, J3.pin5
  N9: Arduino1.D11, J2.pin6
  N10: Arduino1.D13, J2.pin5
  N11: Arduino1.3V3, J2.pin2
  N12: Arduino1.+5V, J1.pin2
  N13: Q3.drain, Q2.source, J4.pin2, D3.cathode, D4.anode
  N14: Q4.drain, Q1.source, D1.anode, J4.pin1, D2.cathode
  N15: Q1.drain, Q2.drain, D1.cathode, D4.cathode
